# Fritzing sketch Schematic (saved by Fritzing 0.8.5b)
breadboards: 1

parts:
  Part1 = Arduino Uno (Rev3)  # not connected
  U1 = Voltage Regulator - 5V [package="TO220 [THT]"]
  VCC1 = 4 x AAA Battery Mount

nets:
  N1: U1.GND, VCC1.-
